# Fritzing sketch IRreceiver (saved by Fritzing 0.9.3b)
breadboards: 1

parts:
  Part1 = Arduino Due (Rev2b)
  IR1 = TSOP312.., 314.. [package=THT]
  LED1 = RGB LED - (4 legs) [package="5 mm [THT]"]
  R1 = Resistor [tolerance=±5% resistance=220 package="2512 [SMD]"]
  R2 = Resistor [tolerance=±5% resistance=220 package="2512 [SMD]"]
  R3 = Resistor [tolerance=±5% resistance=220 package="2512 [SMD]"]

nets:
  N1: Part1.5V, IR1.Vs
  GND: Part1.GND, IR1.GND, LED1.common_anode
  N2: Part1.D9_PWM, R2.Pin_0
  N3: Part1.D10_PWM/SS0, R3.Pin_0
  N4: Part1.D11_PWM, R1.Pin_0
  N5: Part1.D2_PWM, IR1.Data
  N6: LED1.red_cathode, R1.Pin_1
  N7: LED1.green_cathode, R3.Pin_1
  N8: LED1.blue_cathode, R2.Pin_1

notes:
  The IR receiver may look different, but in the included one, the f irst wire should be GND, the second is VCC, and third is Signal Out.
  The RGB LED will have a longer pin; that pin will typically be the pin you should connect to ground.
