# Fritzing sketch Lab 3 (saved by Fritzing 0.9.3b)
breadboards: 1

parts:
  YwRobot_Power_Supply1 = YwRobot Breadboard Power Supply [part_number=545043]
  IC1 = L293D [package=THT]
  S1 = Pushbutton [package="[THT]"]
  Part1 = Arduino Mega 2560 (Rev3)
  M1 = DC Motor
  R1 = Trimmer Potentiometer [maximum_resistance=10kΩ package=THT]
  U1 = LCD-16X2 [package=lcd-16x2]
  R2 = Resistor [tolerance=±5% resistance=10k package=THT]

nets:
  N1: YwRobot_Power_Supply1.VCC#5, R1.leg1, U1.VDD, U1.A
  N2: YwRobot_Power_Supply1.VCC#9, IC1.+V
  GND: YwRobot_Power_Supply1.GND, IC1.0V, S1.Pin_3, S1.Pin_4, Part1.GND, Part1.D2_PWM, R1.leg2, U1.VSS, U1.R_W, U1.K, R2.Pin_0, R2.Pin_1
  N3: IC1.Enable_2, Part1.D5_PWM
  N4: IC1.In_3, Part1.D4_PWM
  N5: IC1.Out_3_(_Controlled_by_Enable_2_), M1.pin_2
  N6: IC1.Out_4_(_Controlled_by_Enable_2_), M1.pin_1
  N7: IC1.In_4, Part1.D3_PWM
  N8: S1.Pin_1, S1.Pin_2, Part1.5V
  N9: Part1.D12_PWM, U1.DB7
  N10: Part1.D11_PWM, U1.DB6
  N11: Part1.D10_PWM, U1.DB5
  N12: Part1.D9_PWM, U1.DB4
  N13: Part1.D8_PWM, U1.E
  N14: Part1.D7_PWM, U1.RS
  N15: R1.wiper, U1.VO

notes:
  10K Resistor

custom parts:
  YwRobot Breadboard Power Supply: The YwRobot Breadboard Power Supply (MB-V2) has two power rails; they can be 5V or 3V3. Power to the module can be provided through the female USB socket or through the A10 (female) 2.1mm power jack.
