# Fritzing sketch SignalProcessingLab (saved by Fritzing 0.9.3b)
breadboards: 1

parts:
  Part1 = Arduino Mega ADK (Rev3)
  LED1 = LED - 5mm [color="Green (555nm)" package="5 mm [THT]"]
  Componente3 = Breakout Board for Electret Microphone
  R1 = Resistor [tolerance=±5% resistance=220 package=THT]
  R2 = Resistor [tolerance=±5% resistance=220 package=THT]
  LED2 = LED - 5mm [color="Green (555nm)" package="5 mm [THT]"]
  R3 = Resistor [tolerance=±5% resistance=220 package=THT]
  LED3 = LED - 5mm [color="Green (555nm)" package="5 mm [THT]"]
  R4 = Resistor [tolerance=±5% resistance=220 package=THT]
  R5 = Resistor [tolerance=±5% resistance=220 package=THT]
  R6 = Resistor [tolerance=±5% resistance=220 package=THT]
  R7 = Resistor [tolerance=±5% resistance=220 package=THT]
  R8 = Resistor [tolerance=±5% resistance=220 package=THT]
  LED4 = LED - 5mm [color="Yellow (585nm)" package="5 mm [THT]"]
  LED5 = LED - 5mm [color="Yellow (585nm)" package="5 mm [THT]"]
  LED6 = LED - 5mm [color="Yellow (585nm)" package="5 mm [THT]"]
  LED7 = LED - 5mm [color="Red (660nm)" package="5 mm [THT]"]
  LED8 = LED - 5mm [color="Red (660nm)" package="5 mm [THT]"]

nets:
  N1: Part1.A0, Componente3.VCC
  GND: Part1.GND, LED1.cathode, Componente3.GND, LED2.cathode, LED3.cathode, LED4.cathode, LED5.cathode, LED6.cathode, LED7.cathode, LED8.cathode
  N2: Part1.D9_PWM, R8.Pin_0
  N3: Part1.D8_PWM, R7.Pin_0
  N4: Part1.5V, Componente3.AUD
  N5: Part1.D2_PWM, R1.Pin_0
  N6: Part1.D3_PWM, R2.Pin_0
  N7: Part1.D4_PWM, R3.Pin_0
  N8: Part1.D5_PWM, R4.Pin_0
  N9: Part1.D6_PWM, R5.Pin_0
  N10: Part1.D7_PWM, R6.Pin_0
  N11: LED1.anode, R1.Pin_1
  N12: R2.Pin_1, LED2.anode
  N13: R3.Pin_1, LED3.anode
  N14: R4.Pin_1, LED4.anode
  N15: R5.Pin_1, LED5.anode
  N16: R6.Pin_1, LED6.anode
  N17: R7.Pin_1, LED7.anode
  N18: R8.Pin_1, LED8.anode

notes:
  On the actual microphone there are 4 inputs, but we will be using 3. Orange is A0, Blue is GND, and Black is 5V.
