# Fritzing sketch TrafficLight (saved by Fritzing 0.9.3b)
breadboards: 3

parts:
  R5 = Resistor [tolerance=±5% resistance=220 package=THT]
  Part1 = Arduino Mega 2560 (Rev3)
  R6 = Resistor [tolerance=±5% resistance=220 package=THT]
  DI1 = 7-Segment LED Display [package=THT]
  R7 = Resistor [tolerance=±5% resistance=330 package=THT]
  LED1 = LED - 5mm [color="Green (570nm)" package="5 mm [THT]"]
  R8 = Resistor [tolerance=±5% resistance=330 package=THT]
  LED2 = LED - 5mm [color="Yellow (595nm)" package="5 mm [THT]"]
  R9 = Resistor [tolerance=±5% resistance=330 package=THT]
  LED3 = LED - 5mm [color="Red (660nm)" package="5 mm [THT]"]
  hc-sr1 = hc-sr04

nets:
  N1: R5.Pin_0, DI1.commAnode#2
  GND: R5.Pin_1, Part1.GND, R6.Pin_1, LED1.cathode, LED2.cathode, LED3.cathode, hc-sr1.GND
  N2: Part1.D13_PWM, hc-sr1.Echo
  N3: Part1.D9_PWM, DI1.cathodeG
  N4: Part1.D8_PWM, DI1.cathodeF
  5V: Part1.5V, hc-sr1.VCC
  N5: Part1.D2_PWM, DI1.cathodeA
  N6: Part1.D3_PWM, DI1.cathodeB
  N7: Part1.D4_PWM, DI1.cathodeC
  N8: Part1.D5_PWM, DI1.cathodeD
  N9: Part1.D6_PWM, DI1.cathodeE
  N10: Part1.D22, R7.Pin_0
  N11: Part1.D24, R8.Pin_0
  N12: Part1.D26, R9.Pin_0
  N13: R6.Pin_0, DI1.commAnode#7
  N14: R7.Pin_1, LED1.anode
  N15: R8.Pin_1, LED2.anode
  N16: R9.Pin_1, LED3.anode
